// Logisim project Georgios_1.circ as structural Verilog: 1 circuit, main circuit main
module main (
  input  [7:0] Store,
  input  [7:0] in_2,
  input  [7:0] in_3,
  input  Clock,
  output [7:0] Result_Register,
  output [7:0] out_6,
  output Carry
);

  wire and_1_out, and_2_out, comparator_1_eq, comparator_2_eq, comparator_3_eq, demultiplexer_2_out0,
       demultiplexer_2_out1, demultiplexer_2_out2, demultiplexer_2_out3, not_1_out;
  wire [1:0] bitselector_1_out;
  wire [7:0] demultiplexer_1_out0, demultiplexer_1_out1, demultiplexer_1_out2, demultiplexer_1_out3,
       multiplexer_1_out, multiplexer_2_out, not_2_out, register_3_q, register_4_q, register_5_q,
       register_6_q;

  Comparator comparator_1 (.a(Store), .b(8'h4), .eq(comparator_1_eq));  // open: gt, lt
  Comparator comparator_2 (.a(Store), .b(8'h3), .eq(comparator_2_eq));  // open: gt, lt
  not not_1 (not_1_out, comparator_3_eq);
  Comparator #(.mode("unsigned")) comparator_3 (.a(Store), .b(8'h1), .eq(comparator_3_eq));  // open: gt, lt
  Comparator #(.mode("unsigned")) comparator_4 (.a(Store), .b(8'h2), .eq(not_1_out));  // open: gt, lt
  assign not_2_out = ~in_3;  // NOT_Gate not_2, 8 bits wide
  Multiplexer #(.width(8)) multiplexer_1 (
    .in0(in_3), .in1(not_2_out), .out(multiplexer_1_out), .sel(not_1_out));  // open: en
  Register register_1 (.D(multiplexer_2_out), .clk(and_1_out));  // open: en, Q, clr
  and and_1 (and_1_out, comparator_1_eq, Clock);
  Adder adder_1 (.a(in_2), .b(multiplexer_1_out), .out(out_6), .cin(not_1_out), .cout(Carry));
  Register register_2 (.D(out_6), .Q(Result_Register), .clk(Clock));  // open: en, clr
  BitSelector #(.group(2)) bitselector_1 (.in(in_2), .out(bitselector_1_out), .sel(2'b00));
  and and_2 (and_2_out, comparator_2_eq, Clock);
  Multiplexer #(.select(2), .width(8), .enable("false")) multiplexer_2 (
    .in0(register_3_q), .in1(register_4_q), .in2(register_5_q), .in3(register_6_q), .out(multiplexer_2_out),
    .sel(bitselector_1_out));
  Demultiplexer #(.select(2), .width(8)) demultiplexer_1 (
    .out0(demultiplexer_1_out0), .out1(demultiplexer_1_out1), .out2(demultiplexer_1_out2),
    .out3(demultiplexer_1_out3), .in(Result_Register), .sel(bitselector_1_out));  // open: en
  Demultiplexer #(.select(2)) demultiplexer_2 (
    .out0(demultiplexer_2_out0), .out1(demultiplexer_2_out1), .out2(demultiplexer_2_out2),
    .out3(demultiplexer_2_out3), .in(and_2_out), .sel(bitselector_1_out));  // open: en
  Register register_3 (.D(demultiplexer_1_out0), .Q(register_3_q), .clk(demultiplexer_2_out0));  // open: en, clr
  Register register_4 (.D(demultiplexer_1_out1), .Q(register_4_q), .clk(demultiplexer_2_out1));  // open: en, clr
  Register register_5 (.D(demultiplexer_1_out2), .Q(register_5_q), .clk(demultiplexer_2_out2));  // open: en, clr
  Register register_6 (.D(demultiplexer_1_out3), .Q(register_6_q), .clk(demultiplexer_2_out3));  // open: en, clr

  // Notes on the sheet:
  //   OP Code
  //   Input A
  //   Input B
  //   Subtract
  //   Load
  //   Add
  //   (incomplete)
  //   Load Register (Goes nowhere)
  //   Georgios 1
  //   Add-Subtract Result
  //   Register 0
  //   Register 1
  //   Register 2
  //   Register 3
endmodule
